# Fritzing sketch BreadBoard (saved by Fritzing 0.9.0b)
breadboards: 1

parts:
  R1 = Resistor [tolerance=±5% resistance=330 package=THT]
  R2 = Resistor [tolerance=±5% resistance=330 package=THT]
  R3 = Resistor [tolerance=±5% resistance=330 package=THT]
  LED1 = LED - 3mm [color="Red (633nm)" package="3 mm [THT]"]
  Componente1 = Arduino Uno (Rev3)
  LED2 = LED - 3mm [color="Red (633nm)" package="3 mm [THT]"]
  LED3 = LED - 3mm [color="Red (633nm)" package="3 mm [THT]"]
  S1 = Pushbutton [package="[THT]"]
  R4 = Resistor [tolerance=±5% resistance=10k package=THT]

nets:
  N1: R1.Pin_0, Componente1.D2
  N2: R1.Pin_1, LED1.cathode
  N3: R2.Pin_0, Componente1.D3_PWM
  N4: R2.Pin_1, LED2.cathode
  N5: R3.Pin_0, Componente1.D4
  N6: R3.Pin_1, LED3.cathode
  N7: LED1.anode, Componente1.GND, LED2.anode, LED3.anode, R4.Pin_1
  N8: Componente1.D5_PWM, S1.Pin_1, S1.Pin_2, R4.Pin_0
  N9: Componente1.5V, S1.Pin_3, S1.Pin_4
