# Fritzing sketch pwm_led (saved by Fritzing 0.9.0b)
breadboards: 1

parts:
  R1 = Resistor [tolerance=±5% resistance=330 package=THT]
  LED1 = LED - 3mm [color="Red (633nm)" package="3 mm [THT]"]
  Componente1 = Arduino Uno (Rev3)
  S1 = Pushbutton [package="[THT]"]
  R4 = Resistor [tolerance=±5% resistance=10k package=THT]
  S2 = Pushbutton [package="[THT]"]
  R5 = Resistor [tolerance=±5% resistance=10k package=THT]

nets:
  N1: R1.Pin_0, Componente1.D5_PWM
  N2: R1.Pin_1, LED1.anode
  N3: LED1.cathode, Componente1.GND, R4.Pin_1, R5.Pin_1
  N4: Componente1.D3_PWM, S1.Pin_1, S1.Pin_2, R4.Pin_0
  N5: Componente1.D4, S2.Pin_1, S2.Pin_2, R5.Pin_0
  N6: Componente1.5V, S1.Pin_3, S1.Pin_4, S2.Pin_3, S2.Pin_4
